// Logisim project minirv32.circ as structural Verilog: 2 circuits, main circuit main
module main (
  input  in_1,
  input  in_2,
  output [31:0] Instruction
);

  wire addi_out, clock_1_out, comparator_1_eq, comparator_2_eq, comparator_3_eq, jalr_out;
  wire [31:0] adder_1_out, adder_2_out, bit_extender_1_out, gprs_1_q0, PC_q;

  Clock clock_1 (.out(clock_1_out));
  ROM #(.addrWidth(16), .dataWidth(32)) rom_1 (.addr(PC_q[17:2]), .data(Instruction));
  Register #(.width(32)) PC (.D(adder_1_out), .en(in_1), .clk(clock_1_out), .Q(PC_q), .clr(in_2));
  Adder #(.width(32)) adder_1 (.a(32'h4), .b(PC_q), .out(adder_1_out));  // open: cin, cout
  GPRs gprs_1 (.clk(clock_1_out), .Q0(gprs_1_q0));  // open: wdata, waddr, WE, raddr0, raddr1, Q1
  Comparator #(.width(7)) comparator_1 (.a(Instruction[6:0]), .b(7'b0010011), .eq(comparator_1_eq));  // open: gt, lt
  Comparator #(.width(3)) comparator_2 (.a(Instruction[14:12]), .b(3'b000), .eq(comparator_2_eq));  // open: gt, lt
  assign bit_extender_1_out = {{20{Instruction[31]}}, Instruction[31:20]};  // Bit_Extender bit_extender_1
  Adder #(.width(32)) adder_2 (.a(bit_extender_1_out), .b(gprs_1_q0), .out(adder_2_out));  // open: cin, cout
  Comparator #(.width(7)) comparator_3 (.a(Instruction[6:0]), .b(7'b1100111), .eq(comparator_3_eq));  // open: gt, lt
  and addi (addi_out, comparator_1_eq, comparator_2_eq);
  and jalr (jalr_out, comparator_2_eq, comparator_3_eq);
  // OR_Gate I has open pins: in0=jalr_out, in1=addi_out, out=open
endmodule

module GPRs (
  input  clk,
  input  [31:0] wdata,
  input  [3:0] waddr,
  input  WE,
  input  [3:0] raddr0,
  input  [3:0] raddr1,
  output [31:0] Q0,
  output [31:0] Q1
);

  wire decoder_1_out1, decoder_1_out2, decoder_1_out3, decoder_1_out4, decoder_1_out5, decoder_1_out6,
       decoder_1_out7, decoder_1_out8, decoder_1_out9, decoder_1_out10, decoder_1_out11, decoder_1_out12,
       decoder_1_out13, decoder_1_out14, decoder_1_out15;
  wire [31:0] register_1_q, register_2_q, register_3_q, register_4_q, register_5_q, register_6_q,
       register_7_q, register_8_q, register_9_q, register_10_q, register_11_q, register_12_q, register_13_q,
       register_14_q, register_15_q, register_16_q;

  Decoder #(.select(4)) decoder_1 (
    .out1(decoder_1_out1), .out2(decoder_1_out2), .out3(decoder_1_out3), .out4(decoder_1_out4),
    .out5(decoder_1_out5), .out6(decoder_1_out6), .out7(decoder_1_out7), .out8(decoder_1_out8),
    .out9(decoder_1_out9), .out10(decoder_1_out10), .out11(decoder_1_out11), .out12(decoder_1_out12),
    .out13(decoder_1_out13), .out14(decoder_1_out14), .out15(decoder_1_out15), .sel(waddr), .en(WE));  // open: out0
  Register #(.width(32)) register_1 (.D(wdata), .en(decoder_1_out1), .clk(clk), .Q(register_1_q));  // open: clr
  Register #(.width(32)) register_2 (.D(wdata), .en(decoder_1_out8), .clk(clk), .Q(register_2_q));  // open: clr
  Register #(.width(32)) register_3 (.D(wdata), .en(decoder_1_out1), .clk(clk), .Q(register_3_q));  // open: clr
  Register #(.width(32)) register_4 (.D(wdata), .en(decoder_1_out9), .clk(clk), .Q(register_4_q));  // open: clr
  Register #(.width(32)) register_5 (.D(wdata), .en(decoder_1_out2), .clk(clk), .Q(register_5_q));  // open: clr
  Register #(.width(32)) register_6 (.D(wdata), .en(decoder_1_out10), .clk(clk), .Q(register_6_q));  // open: clr
  Register #(.width(32)) register_7 (.D(wdata), .en(decoder_1_out3), .clk(clk), .Q(register_7_q));  // open: clr
  Register #(.width(32)) register_8 (.D(wdata), .en(decoder_1_out11), .clk(clk), .Q(register_8_q));  // open: clr
  Register #(.width(32)) register_9 (.D(wdata), .en(decoder_1_out4), .clk(clk), .Q(register_9_q));  // open: clr
  Register #(.width(32)) register_10 (.D(wdata), .en(decoder_1_out12), .clk(clk), .Q(register_10_q));  // open: clr
  Register #(.width(32)) register_11 (.D(wdata), .en(decoder_1_out5), .clk(clk), .Q(register_11_q));  // open: clr
  Register #(.width(32)) register_12 (.D(wdata), .en(decoder_1_out13), .clk(clk), .Q(register_12_q));  // open: clr
  Register #(.width(32)) register_13 (.D(wdata), .en(decoder_1_out6), .clk(clk), .Q(register_13_q));  // open: clr
  Register #(.width(32)) register_14 (.D(wdata), .en(decoder_1_out14), .clk(clk), .Q(register_14_q));  // open: clr
  Register #(.width(32)) register_15 (.D(wdata), .en(decoder_1_out7), .clk(clk), .Q(register_15_q));  // open: clr
  Register #(.width(32)) register_16 (.D(wdata), .en(decoder_1_out15), .clk(clk), .Q(register_16_q));  // open: clr
  Multiplexer #(.select(4), .width(32)) multiplexer_1 (
    .in0(register_1_q), .in1(register_3_q), .in2(register_5_q), .in3(register_7_q), .in4(register_9_q),
    .in5(register_11_q), .in6(register_13_q), .in7(register_15_q), .in8(register_2_q), .in9(register_4_q),
    .in10(register_6_q), .in11(register_8_q), .in12(register_10_q), .in13(register_12_q),
    .in14(register_14_q), .in15(register_16_q), .out(Q0), .sel(raddr0));
  Multiplexer #(.select(4), .width(32)) multiplexer_2 (
    .in0(register_1_q), .in1(register_3_q), .in2(register_5_q), .in3(register_7_q), .in4(register_9_q),
    .in5(register_11_q), .in6(register_13_q), .in7(register_15_q), .in8(register_2_q), .in9(register_4_q),
    .in10(register_6_q), .in11(register_8_q), .in12(register_10_q), .in13(register_12_q),
    .in14(register_14_q), .in15(register_16_q), .out(Q1), .sel(raddr1));
endmodule
